# Fritzing sketch Untitled Sketch 2 (saved by Fritzing 0.8.7b)
breadboards: 1

parts:
  U2 = Module 4 Relais 5V [package="Module 4 Relais 5V"]
  R1 = Temperature Sensor (Thermistor) [thermistor_type=NTC package=THT]
  Part1 = Lilypad Battery Connect
  R2 = Heating Pad
  WATER_PUMP1 = water pump/motor
  U3 = HIH-4030 [package=hih-4030]
  S1 = Pushbutton [package="[THT]"]
  S2 = Pushbutton [package="[THT]"]
  S3 = Pushbutton [package="[THT]"]
  LED1 = LED - 5mm [color="Red (633nm)" package="5 mm [THT]"]
  Raspberry_Pi_1 = Raspberry Pi 3

nets:
  VCC: U2.VCC, Raspberry_Pi_1.5V
  GND: U2.GND, R1.pin_1, U3.GND, S2.Pin_1, S2.Pin_2, S3.Pin_1, S3.Pin_2, LED1.cathode, LED1.anode, Raspberry_Pi_1.GIPO19, Raspberry_Pi_1.GND
  N1: U2.IN1, Raspberry_Pi_1.GIPO14
  N2: U2.IN2, Raspberry_Pi_1.GIPO15
  N3: U2.K1-NF, WATER_PUMP1.pin_2
  N4: U2.K2-NF, R2.pin_1
  N5: U2.K1-NO, U2.K2-NO, Part1.+
  N6: R1.pin_0, Raspberry_Pi_1.GIPO5
  N7: Part1.-, R2.pin_0, WATER_PUMP1.pin_1
  N8: U3.VCC, Raspberry_Pi_1.GIPO12
  N9: S1.Pin_1, S1.Pin_2
  N10: S1.Pin_3, S1.Pin_4, Raspberry_Pi_1.GIPO6
  N11: S2.Pin_3, S2.Pin_4, Raspberry_Pi_1.GIPO13
  N12: S3.Pin_3, S3.Pin_4, Raspberry_Pi_1.GIPO16

notes:
  Waterpump 230V
  Heat chamber 230V

custom parts:
  Module 4 Relais 5V: Module 4 Relais 5V 4x SPD-06VDC-SD-C
  Heating Pad: A thermoresistant material with an embeded conductor that dissipates electrical energy into heat.
  water pump/motor: WATER PUMP BY ARDUBLOCKTR
